# Fritzing sketch load_cell_schematic (saved by Fritzing 1.0.1rc)
breadboards: 1

parts:
  HX711 = HX711 Weighing Sensor Module
  Display_I2C = LCD1602-I2C
  Componente4 = Arduino Nano (Rev3.0)
  Load_Cell = Load Cell - Red/white/black/green
  Sensor1 = TTP223B Capacitive Touch Sensor Module

nets:
  VCC: HX711.VCC, Display_I2C.VCC, Componente4.5V, Sensor1.VCC
  GND: HX711.GND, Display_I2C.GND, Componente4.GND, Sensor1.GND
  N1: HX711.DO/RX, Componente4.D4
  N2: HX711.CK/TX, Componente4.D3
  N3: HX711.E+, Load_Cell.wire1
  N4: HX711.E-, Load_Cell.wire3
  N5: HX711.A+, Load_Cell.wire2
  N6: HX711.A-, Load_Cell.wire4
  N7: Display_I2C.SDA, Componente4.A4
  N8: Display_I2C.SCL, Componente4.A5
  N9: Componente4.D5, Sensor1.SIG

custom parts:
  HX711 Weighing Sensor Module: HX711 is a precision 24-bit analog-to-digital converter (ADC) designed for weigh scales and industrial control applications to interface directly with a bridge sensor.
  LCD1602-I2C: A standard character display, usually with 2x16 characters. Comes in many colors with LCM1602 IIC attached.
  Load Cell - Red/white/black/green: A rectangle load cell/weighting pressure Sensor with four wires - Red, white, black, green. Normally corresponding with E+, E-, A+, A- respectively.
  TTP223B Capacitive Touch Sensor Module: The TTP223B capacitive touch sensor module uses the TTP223B IC. The appropriate voltage is approximately 2 to 5.5 volts.
